// Logisim project main.circ as structural Verilog
module main (
  input  in_1,
  input  in_2,
  input  in_3,
  input  in_4,
  input  [7:0] in_5,
  input  in_6,
  input  [2:0] in_7,
  input  [2:0] in_8,
  input  [7:0] in_9,
  output [7:0] out_10,
  output [7:0] out_11
);

  wire adder_8_1_co, clock_1_out, clock_2_out, clock_3_out, d_rising_edge_flipflop_1_q;
  wire [7:0] adder_8_1_s, d_rising_edge_flipflop_8_1_do;

  Clock clock_1 (.out(clock_1_out));
  adder_8 adder_8_1 (.A(8'h1), .B(8'h2), .CI(in_1), .S(adder_8_1_s), .CO(adder_8_1_co));
  D_rising_edge_flipflop d_rising_edge_flipflop_1 (
    .D(in_2), .CP(clock_1_out), .Q(d_rising_edge_flipflop_1_q));  // open: Clear, Preset, Q_bar
  Clock clock_2 (.out(clock_2_out));
  Clock clock_3 (.out(clock_3_out));
  LED led_1 (.in(d_rising_edge_flipflop_1_q));
  D_rising_edge_flipflop_8 d_rising_edge_flipflop_8_1 (
    .DI(in_5), .Preset(in_3), .Clear(in_6), .CP(clock_2_out), .DO(d_rising_edge_flipflop_8_1_do));
  byte_8_register byte_8_register_1 (
    .R(in_7), .W(in_8), .DI(in_9), .CP(clock_3_out), .out_7(out_11));  // open: Preset, Clear
  tri_state_gate_8 tri_state_gate_8_1 (.EN(in_4), .I(d_rising_edge_flipflop_8_1_do), .O(out_10));
  LED led_2 (.in(adder_8_1_s[0]));
  LED led_3 (.in(adder_8_1_s[1]));
  LED led_4 (.in(adder_8_1_s[2]));
  LED led_5 (.in(adder_8_1_s[3]));
  LED led_6 (.in(adder_8_1_s[4]));
  LED led_7 (.in(adder_8_1_s[5]));
  LED led_8 (.in(adder_8_1_s[6]));
  LED led_9 (.in(adder_8_1_s[7]));
  LED led_10 (.in(adder_8_1_co));
endmodule

// HA
module half_adder (
  input  A,
  input  B,
  output S,
  output C
);

  xor xor_1 (S, B, A);
  and and_1 (C, A, B);
endmodule

// FA
module full_adder (
  input  CI,
  input  A,
  input  B,
  output S,
  output CO
);

  wire half_adder_1_c, half_adder_1_s, half_adder_2_c;

  half_adder half_adder_1 (.A(A), .B(B), .C(half_adder_1_c), .S(half_adder_1_s));
  half_adder half_adder_2 (.A(CI), .B(half_adder_1_s), .C(half_adder_2_c), .S(S));
  or or_1 (CO, half_adder_2_c, half_adder_1_c);
endmodule

// 8A
module adder_8 (
  input  CI,
  input  [7:0] A,
  input  [7:0] B,
  output [7:0] S,
  output CO
);

  wire full_adder_2_co, full_adder_3_co, full_adder_4_co, full_adder_5_co, full_adder_6_co, full_adder_7_co,
       full_adder_8_co;

  full_adder full_adder_1 (.CI(full_adder_2_co), .A(A[7]), .B(B[7]), .S(S[7]), .CO(CO));
  full_adder full_adder_2 (.CI(full_adder_3_co), .A(A[6]), .B(B[6]), .S(S[6]), .CO(full_adder_2_co));
  full_adder full_adder_3 (.CI(full_adder_4_co), .A(A[5]), .B(B[5]), .S(S[5]), .CO(full_adder_3_co));
  full_adder full_adder_4 (.CI(full_adder_5_co), .A(A[4]), .B(B[4]), .S(S[4]), .CO(full_adder_4_co));
  full_adder full_adder_5 (.CI(full_adder_6_co), .A(A[3]), .B(B[3]), .S(S[3]), .CO(full_adder_5_co));
  full_adder full_adder_6 (.CI(full_adder_7_co), .A(A[2]), .B(B[2]), .S(S[2]), .CO(full_adder_6_co));
  full_adder full_adder_7 (.CI(full_adder_8_co), .A(A[1]), .B(B[1]), .S(S[1]), .CO(full_adder_7_co));
  full_adder full_adder_8 (.CI(CI), .A(A[0]), .B(B[0]), .S(S[0]), .CO(full_adder_8_co));
endmodule

// RS
module S_R_flipflop (
  input  Preset,
  input  S,
  input  R,
  input  Clear,
  output Q,
  output Q_bar
);

  wire or_1_out, or_2_out, or_3_out, or_4_out;

  or or_1 (or_1_out, Preset, S);
  or or_2 (or_2_out, R, Clear);
  or or_3 (or_3_out, or_1_out, Q);
  or or_4 (or_4_out, Q_bar, or_2_out);
  not not_1 (Q_bar, or_3_out);
  not not_2 (Q, or_4_out);
endmodule

// D
module D_flipflop (
  input  D,
  input  Preset,
  input  EN,
  input  Clear,
  output Q,
  output Q_bar
);

  wire and_1_out, and_2_out, not_1_out;

  and and_1 (and_1_out, D, EN);
  and and_2 (and_2_out, EN, not_1_out);
  not not_1 (not_1_out, D);
  S_R_flipflop s_r_flipflop_1 (.S(and_1_out), .R(and_2_out), .Clear(Clear), .Preset(Preset), .Q(Q), .Q_bar(Q_bar));
endmodule

// D>
module D_rising_edge_flipflop (
  input  Preset,
  input  D,
  input  CP,
  input  Clear,
  output Q,
  output Q_bar
);

  wire d_flipflop_1_q, not_1_out;

  D_flipflop d_flipflop_1 (.EN(not_1_out), .D(D), .Clear(Clear), .Preset(Preset), .Q(d_flipflop_1_q));  // open: Q_bar
  not not_1 (not_1_out, CP);
  D_flipflop d_flipflop_2 (.EN(CP), .D(d_flipflop_1_q), .Clear(Clear), .Preset(Preset), .Q(Q), .Q_bar(Q_bar));
endmodule

// T>
module T_rising_edge_flipflop (
  input  Preset,
  input  CP,
  input  Clear,
  output Q,
  output Q_bar
);

  D_rising_edge_flipflop d_rising_edge_flipflop_1 (
    .D(Q_bar), .CP(CP), .Clear(Clear), .Preset(Preset), .Q(Q), .Q_bar(Q_bar));
endmodule

// RA
module ripple_counter (
  input  PS,
  input  CP,
  input  CLR,
  output [7:0] Q
);

  wire t_rising_edge_flipflop_1_q_bar, t_rising_edge_flipflop_2_q_bar, t_rising_edge_flipflop_3_q_bar,
       t_rising_edge_flipflop_4_q_bar, t_rising_edge_flipflop_5_q_bar, t_rising_edge_flipflop_6_q_bar,
       t_rising_edge_flipflop_7_q_bar;

  T_rising_edge_flipflop t_rising_edge_flipflop_1 (
    .CP(CP), .Preset(PS), .Clear(CLR), .Q(Q[7]), .Q_bar(t_rising_edge_flipflop_1_q_bar));
  T_rising_edge_flipflop t_rising_edge_flipflop_2 (
    .CP(t_rising_edge_flipflop_1_q_bar), .Preset(PS), .Clear(CLR), .Q(Q[6]),
    .Q_bar(t_rising_edge_flipflop_2_q_bar));
  T_rising_edge_flipflop t_rising_edge_flipflop_3 (
    .CP(t_rising_edge_flipflop_2_q_bar), .Preset(PS), .Clear(CLR), .Q(Q[5]),
    .Q_bar(t_rising_edge_flipflop_3_q_bar));
  T_rising_edge_flipflop t_rising_edge_flipflop_4 (
    .CP(t_rising_edge_flipflop_3_q_bar), .Preset(PS), .Clear(CLR), .Q(Q[4]),
    .Q_bar(t_rising_edge_flipflop_4_q_bar));
  T_rising_edge_flipflop t_rising_edge_flipflop_5 (
    .CP(t_rising_edge_flipflop_4_q_bar), .Preset(PS), .Clear(CLR), .Q(Q[3]),
    .Q_bar(t_rising_edge_flipflop_5_q_bar));
  T_rising_edge_flipflop t_rising_edge_flipflop_6 (
    .CP(t_rising_edge_flipflop_5_q_bar), .Preset(PS), .Clear(CLR), .Q(Q[2]),
    .Q_bar(t_rising_edge_flipflop_6_q_bar));
  T_rising_edge_flipflop t_rising_edge_flipflop_7 (
    .CP(t_rising_edge_flipflop_6_q_bar), .Preset(PS), .Clear(CLR), .Q(Q[1]),
    .Q_bar(t_rising_edge_flipflop_7_q_bar));
  T_rising_edge_flipflop t_rising_edge_flipflop_8 (
    .CP(t_rising_edge_flipflop_7_q_bar), .Preset(PS), .Clear(CLR), .Q(Q[0]));  // open: Q_bar
endmodule

// 8D
module D_rising_edge_flipflop_8 (
  input  [7:0] DI,
  input  Preset,
  input  Clear,
  input  CP,
  output [7:0] DO
);

  D_rising_edge_flipflop d_rising_edge_flipflop_1 (
    .D(DI[7]), .CP(CP), .Clear(Clear), .Preset(Preset), .Q(DO[7]));  // open: Q_bar
  D_rising_edge_flipflop d_rising_edge_flipflop_2 (
    .D(DI[6]), .CP(CP), .Clear(Clear), .Preset(Preset), .Q(DO[6]));  // open: Q_bar
  D_rising_edge_flipflop d_rising_edge_flipflop_3 (
    .D(DI[5]), .CP(CP), .Clear(Clear), .Preset(Preset), .Q(DO[5]));  // open: Q_bar
  D_rising_edge_flipflop d_rising_edge_flipflop_4 (
    .D(DI[4]), .CP(CP), .Clear(Clear), .Preset(Preset), .Q(DO[4]));  // open: Q_bar
  D_rising_edge_flipflop d_rising_edge_flipflop_5 (
    .D(DI[3]), .CP(CP), .Clear(Clear), .Preset(Preset), .Q(DO[3]));  // open: Q_bar
  D_rising_edge_flipflop d_rising_edge_flipflop_6 (
    .D(DI[2]), .CP(CP), .Clear(Clear), .Preset(Preset), .Q(DO[2]));  // open: Q_bar
  D_rising_edge_flipflop d_rising_edge_flipflop_7 (
    .D(DI[1]), .CP(CP), .Clear(Clear), .Preset(Preset), .Q(DO[1]));  // open: Q_bar
  D_rising_edge_flipflop d_rising_edge_flipflop_8 (
    .D(DI[0]), .CP(CP), .Clear(Clear), .Preset(Preset), .Q(DO[0]));  // open: Q_bar
endmodule

// 8GATE
module tri_state_gate_8 (
  input  EN,
  input  [7:0] I,
  output [7:0] O
);

  wire not_1_out;

  not not_1 (not_1_out, EN);
  Transistor transistor_1 (.in(I[0]), .out(O[0]), .gate(not_1_out));
  Transistor transistor_2 (.in(I[1]), .out(O[1]), .gate(not_1_out));
  Transistor transistor_3 (.in(I[2]), .out(O[2]), .gate(not_1_out));
  Transistor transistor_4 (.in(I[3]), .out(O[3]), .gate(not_1_out));
  Transistor transistor_5 (.in(I[4]), .out(O[4]), .gate(not_1_out));
  Transistor transistor_6 (.in(I[5]), .out(O[5]), .gate(not_1_out));
  Transistor transistor_7 (.in(I[6]), .out(O[6]), .gate(not_1_out));
  Transistor transistor_8 (.in(I[7]), .out(O[7]), .gate(not_1_out));
endmodule

// BYTE
module byte_register (
  input  [7:0] DI,
  input  Preset,
  input  R,
  input  CP,
  input  W,
  input  Clear,
  output [7:0] DO
);

  wire and_1_out;
  wire [7:0] d_rising_edge_flipflop_8_1_do;

  and and_1 (and_1_out, CP, W);
  D_rising_edge_flipflop_8 d_rising_edge_flipflop_8_1 (
    .DI(DI), .Preset(Preset), .Clear(Clear), .CP(and_1_out), .DO(d_rising_edge_flipflop_8_1_do));
  tri_state_gate_8 tri_state_gate_8_1 (.EN(R), .I(d_rising_edge_flipflop_8_1_do), .O(DO));
endmodule

// 3-8DEC
module three_to_eight_decoder (
  input  A1,
  input  A2,
  input  A3,
  output [7:0] O
);

  wire and_1_out, and_3_out, and_5_out, and_7_out, and_9_out, and_11_out, and_13_out, and_15_out, not_1_out,
       not_2_out, not_3_out;

  not not_1 (not_1_out, A1);
  not not_2 (not_2_out, A2);
  not not_3 (not_3_out, A3);
  and and_1 (and_1_out, not_1_out, not_2_out);
  and and_2 (O[0], and_1_out, not_3_out);
  and and_3 (and_3_out, A1, not_2_out);
  and and_4 (O[1], and_3_out, not_3_out);
  and and_5 (and_5_out, not_1_out, A2);
  and and_6 (O[2], and_5_out, not_3_out);
  and and_7 (and_7_out, A1, A2);
  and and_8 (O[3], and_7_out, not_3_out);
  and and_9 (and_9_out, not_1_out, not_2_out);
  and and_10 (O[4], and_9_out, A3);
  and and_11 (and_11_out, A1, not_2_out);
  and and_12 (O[5], and_11_out, A3);
  and and_13 (and_13_out, not_1_out, A3);
  and and_14 (O[6], and_13_out, A2);
  and and_15 (and_15_out, A1, A2);
  and and_16 (O[7], and_15_out, A3);
endmodule

// BYTE-8
module byte_8_register (
  input  [2:0] R,
  input  [2:0] W,
  input  [7:0] DI,
  input  CP,
  input  Preset,
  input  Clear,
  output [7:0] out_7
);

  wire [7:0] three_to_eight_decoder_1_o, three_to_eight_decoder_2_o;

  three_to_eight_decoder three_to_eight_decoder_1 (.A2(R[1]), .A3(R[2]), .A1(R[0]), .O(three_to_eight_decoder_1_o));
  three_to_eight_decoder three_to_eight_decoder_2 (.A2(W[1]), .A3(W[2]), .A1(W[0]), .O(three_to_eight_decoder_2_o));
  byte_register byte_register_1 (
    .CP(CP), .W(three_to_eight_decoder_2_o[7]), .DI(DI), .Preset(Preset), .Clear(Clear),
    .R(three_to_eight_decoder_1_o[7]), .DO(out_7));
  byte_register byte_register_2 (
    .CP(CP), .W(three_to_eight_decoder_2_o[6]), .DI(DI), .Preset(Preset), .Clear(Clear),
    .R(three_to_eight_decoder_1_o[6]), .DO(out_7));
  byte_register byte_register_3 (
    .CP(CP), .W(three_to_eight_decoder_2_o[5]), .DI(DI), .Preset(Preset), .Clear(Clear),
    .R(three_to_eight_decoder_1_o[5]), .DO(out_7));
  byte_register byte_register_4 (
    .CP(CP), .W(three_to_eight_decoder_2_o[4]), .DI(DI), .Preset(Preset), .Clear(Clear),
    .R(three_to_eight_decoder_1_o[4]), .DO(out_7));
  byte_register byte_register_5 (
    .CP(CP), .W(three_to_eight_decoder_2_o[3]), .DI(DI), .Preset(Preset), .Clear(Clear),
    .R(three_to_eight_decoder_1_o[3]), .DO(out_7));
  byte_register byte_register_6 (
    .CP(CP), .W(three_to_eight_decoder_2_o[2]), .DI(DI), .Preset(Preset), .Clear(Clear),
    .R(three_to_eight_decoder_1_o[2]), .DO(out_7));
  byte_register byte_register_7 (
    .CP(CP), .W(three_to_eight_decoder_2_o[1]), .DI(DI), .Preset(Preset), .Clear(Clear),
    .R(three_to_eight_decoder_1_o[1]), .DO(out_7));
  byte_register byte_register_8 (
    .CP(CP), .W(three_to_eight_decoder_2_o[0]), .DI(DI), .Preset(Preset), .Clear(Clear),
    .R(three_to_eight_decoder_1_o[0]), .DO(out_7));
endmodule

module byte_16_bit_ext_register (
  input  [2:0] R,
  input  [2:0] W,
  input  [15:0] DI,
  input  CP,
  input  Preset,
  input  Clear,
  output [15:0] DO
);

  byte_8_register byte_8_register_1 (
    .R(R), .W(W), .DI(DI[15:8]), .CP(CP), .Preset(Preset), .Clear(Clear), .out_7(DO[15:8]));
  byte_8_register byte_8_register_2 (
    .R(R), .W(W), .DI(DI[7:0]), .CP(CP), .Preset(Preset), .Clear(Clear), .out_7(DO[7:0]));

  // Notes on the sheet:
  //   位扩展
endmodule
